// Logisim project logisim.circ as structural Verilog: 5 circuits, main circuit Final Circuit
module Final_Circuit (
  input  in_1,
  input  Input_Buttons,
  input  in_3,
  input  in_4,
  input  in_5,
  input  in_6
);

  wire clock_1_out, clock_2_out, comparator_1_out_9, counter_1_carry, counter_2_carry, d_ff_1_q, d_ff_2_q,
       d_ff_3_q, d_ff_4_q, d_ff_5_q, d_ff_6_q, d_ff_7_q, d_ff_8_q, d_ff_9_q, d_ff_9_qn,
       multiplexer_logic_1_out_10, multiplexer_logic_1_out_11, multiplexer_logic_1_out_12,
       multiplexer_logic_1_out_13, xor_1_out;

  D_Flip_Flop d_ff_1 (.clk(clock_2_out), .D(d_ff_2_q), .Q(d_ff_1_q));  // open: Qn, preset, en, reset
  D_Flip_Flop d_ff_2 (
    .clk(clock_2_out), .D(xor_1_out), .Q(d_ff_2_q), .en(comparator_1_out_9));  // open: Qn, preset, reset
  xor xor_1 (xor_1_out, d_ff_7_q, d_ff_5_q);
  D_Flip_Flop d_ff_3 (
    .clk(clock_2_out), .D(d_ff_2_q), .Q(d_ff_3_q), .en(comparator_1_out_9));  // open: Qn, preset, reset
  D_Flip_Flop d_ff_4 (.clk(clock_2_out), .D(d_ff_3_q), .Q(d_ff_4_q));  // open: Qn, preset, en, reset
  D_Flip_Flop d_ff_5 (
    .clk(clock_2_out), .D(d_ff_3_q), .Q(d_ff_5_q), .en(comparator_1_out_9));  // open: Qn, preset, reset
  D_Flip_Flop d_ff_6 (.clk(clock_2_out), .D(d_ff_5_q), .Q(d_ff_6_q));  // open: Qn, preset, en, reset
  D_Flip_Flop d_ff_7 (
    .clk(clock_2_out), .D(d_ff_5_q), .Q(d_ff_7_q), .en(comparator_1_out_9));  // open: Qn, preset, reset
  D_Flip_Flop d_ff_8 (.clk(clock_2_out), .D(d_ff_7_q), .Q(d_ff_8_q));  // open: Qn, preset, en, reset
  Clock clock_1 (.out(clock_1_out));
  D_Flip_Flop d_ff_9 (.clk(clock_1_out), .D(d_ff_9_qn), .Q(d_ff_9_q), .Qn(d_ff_9_qn));  // open: preset, en, reset
  Multiplexer_Logic multiplexer_logic_1 (
    .in_1(d_ff_2_q), .in_2(d_ff_1_q), .in_3(d_ff_3_q), .in_4(d_ff_4_q), .in_5(d_ff_5_q), .in_6(d_ff_6_q),
    .in_7(d_ff_7_q), .in_8(d_ff_8_q), .out_10(multiplexer_logic_1_out_10),
    .out_11(multiplexer_logic_1_out_11), .out_12(multiplexer_logic_1_out_12),
    .out_13(multiplexer_logic_1_out_13), .in_9(d_ff_9_qn));
  LED led_1 (.in(d_ff_9_q));
  LED led_2 (.in(d_ff_9_qn));
  LED led_3 (.in(d_ff_3_q));
  LED led_4 (.in(d_ff_2_q));
  LED led_5 (.in(d_ff_7_q));
  LED led_6 (.in(d_ff_5_q));
  Clock clock_2 (.out(clock_2_out));
  Comparator comparator_1 (
    .in_1(multiplexer_logic_1_out_10), .in_2(in_1), .in_3(multiplexer_logic_1_out_11), .in_4(Input_Buttons),
    .in_5(multiplexer_logic_1_out_12), .in_6(in_3), .in_7(multiplexer_logic_1_out_13), .in_8(in_4),
    .out_9(comparator_1_out_9));
  LED led_7 (.in(counter_2_carry));
  Counter #(.width(3), .max('h3)) counter_1 (
    .carry(counter_1_carry), .clk(comparator_1_out_9), .clr(in_5));  // open: load, D, count, Q
  Counter #(.width(3), .max('h4)) counter_2 (
    .carry(counter_2_carry), .clk(counter_1_carry), .clr(in_6));  // open: load, D, count, Q

  // Notes on the sheet:
  //   Random Number Generator
  //   Second Set of D Flip Flops to store previous sequence
  //   GAME INSTRUCTIONS:
  //   2. After inputting, press the OK button.
  //   4. If you reach the high score(15) (displayed by the counter), you win!
  //   to input the right answer, and will not change until you enter the right input.
  //   Remember The Bits!
  //   Multiplexer Logic
  //   Display prompting user on 
  //   which sequence to input
  //   When the bottom light is on and top light is off, input the previous sequence to score a point
  //   3. If you enter the wrong input, the LED sequence does not change, giving you a second chance
  //   1. When the top light of the left display is on and bottom light is off, you have to input the current sequence 
  //   Current Sequence
  //   4 Bit Comparator
  //   LED to indicate victory!
  //   OK
  //   Score in a level.
  //   Level
endmodule

module Final_Without_Sub (
  input  in_1,
  input  Input_Buttons,
  input  in_3,
  input  in_4,
  input  in_5,
  input  in_6
);

  wire and_1_out, clock_1_out, clock_2_out, counter_1_carry, counter_2_carry, d_ff_1_q, d_ff_2_q, d_ff_3_q,
       d_ff_4_q, d_ff_5_q, d_ff_6_q, d_ff_7_q, d_ff_8_q, d_ff_9_q, d_ff_9_qn, multiplexer_1_out,
       multiplexer_2_out, multiplexer_3_out, multiplexer_4_out, xnor_1_out, xnor_2_out, xnor_3_out,
       xnor_4_out, xor_1_out;

  D_Flip_Flop d_ff_1 (.clk(clock_2_out), .D(d_ff_2_q), .Q(d_ff_1_q));  // open: Qn, preset, en, reset
  D_Flip_Flop d_ff_2 (.clk(clock_2_out), .D(xor_1_out), .Q(d_ff_2_q), .en(and_1_out));  // open: Qn, preset, reset
  xor xor_1 (xor_1_out, d_ff_7_q, d_ff_5_q);
  D_Flip_Flop d_ff_3 (.clk(clock_2_out), .D(d_ff_2_q), .Q(d_ff_3_q), .en(and_1_out));  // open: Qn, preset, reset
  D_Flip_Flop d_ff_4 (.clk(clock_2_out), .D(d_ff_3_q), .Q(d_ff_4_q));  // open: Qn, preset, en, reset
  D_Flip_Flop d_ff_5 (.clk(clock_2_out), .D(d_ff_3_q), .Q(d_ff_5_q), .en(and_1_out));  // open: Qn, preset, reset
  D_Flip_Flop d_ff_6 (.clk(clock_2_out), .D(d_ff_5_q), .Q(d_ff_6_q));  // open: Qn, preset, en, reset
  D_Flip_Flop d_ff_7 (.clk(clock_2_out), .D(d_ff_5_q), .Q(d_ff_7_q), .en(and_1_out));  // open: Qn, preset, reset
  D_Flip_Flop d_ff_8 (.clk(clock_2_out), .D(d_ff_7_q), .Q(d_ff_8_q));  // open: Qn, preset, en, reset
  Clock clock_1 (.out(clock_1_out));
  D_Flip_Flop d_ff_9 (.clk(clock_1_out), .D(d_ff_9_qn), .Q(d_ff_9_q), .Qn(d_ff_9_qn));  // open: preset, en, reset
  Multiplexer multiplexer_1 (.in0(d_ff_2_q), .in1(d_ff_1_q), .out(multiplexer_1_out), .sel(d_ff_9_qn));  // open: en
  Multiplexer multiplexer_2 (.in0(d_ff_3_q), .in1(d_ff_4_q), .out(multiplexer_2_out), .sel(d_ff_9_qn));  // open: en
  Multiplexer multiplexer_3 (.in0(d_ff_5_q), .in1(d_ff_6_q), .out(multiplexer_3_out), .sel(d_ff_9_qn));  // open: en
  Multiplexer multiplexer_4 (.in0(d_ff_7_q), .in1(d_ff_8_q), .out(multiplexer_4_out), .sel(d_ff_9_qn));  // open: en
  LED led_1 (.in(d_ff_9_q));
  LED led_2 (.in(d_ff_9_qn));
  LED led_3 (.in(d_ff_7_q));
  LED led_4 (.in(d_ff_2_q));
  LED led_5 (.in(d_ff_5_q));
  LED led_6 (.in(d_ff_3_q));
  Clock clock_2 (.out(clock_2_out));
  LED led_7 (.in(counter_2_carry));
  xnor xnor_1 (xnor_1_out, multiplexer_1_out, in_1);
  xnor xnor_2 (xnor_2_out, multiplexer_2_out, Input_Buttons);
  xnor xnor_3 (xnor_3_out, multiplexer_3_out, in_3);
  xnor xnor_4 (xnor_4_out, multiplexer_4_out, in_4);
  and and_1 (and_1_out, xnor_1_out, xnor_2_out, xnor_3_out, xnor_4_out);
  Counter #(.width(3), .max('h3)) counter_1 (
    .carry(counter_1_carry), .clk(and_1_out), .clr(in_5));  // open: load, D, count, Q
  Counter #(.width(3), .max('h4)) counter_2 (
    .carry(counter_2_carry), .clk(counter_1_carry), .clr(in_6));  // open: load, D, count, Q

  // Notes on the sheet:
  //   Random Number Generator
  //   Second Set of D Flip Flops to store previous sequence
  //   INSTRUCTIONS:
  //   2. After inputting, press the OK button.
  //   4. If you reach the high score(15) (displayed by the counter), you win!
  //   to input the right answer, and will not change until you enter the right input.
  //   Display prompting user on 
  //   which sequence to input
  //   When the bottom light is on and top light is off, input the previous sequence to score a point
  //   3. If you enter the wrong input, the LED sequence does not change, giving you a second chance
  //   4 Multiplexers to decide which sequence to be compared 
  //   with user input based on 2 LED Display
  //   1. When the top light of the left display is on and bottom light is off, you have to input the current sequence 
  //   Remember The Bits!
  //   Current Sequence
  //   LED to indicate victory!
  //   OK
  //   4 Bit Comparator
  //   Score in a level.
  //   Level
endmodule

module Scoreboard (
  input  in_1
);

  wire clock_1_out, counter_1_carry, counter_2_carry;

  Clock clock_1 (.out(clock_1_out));
  Counter #(.width(3), .max('h3)) counter_1 (
    .carry(counter_1_carry), .clk(clock_1_out), .clr(in_1));  // open: load, D, count, Q
  Counter #(.width(3), .max('h4)) counter_2 (
    .carry(counter_2_carry), .clk(counter_1_carry));  // open: load, D, count, Q, clr
  LED led_1 (.in(counter_2_carry));

  // Notes on the sheet:
  //   Score in a level.
  //   Level
  //   Indicates whether the player won 
endmodule

module Comparator (
  input  in_1,
  input  in_2,
  input  in_3,
  input  in_4,
  input  in_5,
  input  in_6,
  input  in_7,
  input  in_8,
  output out_9
);

  wire xnor_1_out, xnor_2_out, xnor_3_out, xnor_4_out;

  xnor xnor_1 (xnor_1_out, in_1, in_2);
  xnor xnor_2 (xnor_2_out, in_3, in_4);
  xnor xnor_3 (xnor_3_out, in_5, in_6);
  xnor xnor_4 (xnor_4_out, in_7, in_8);
  and and_1 (out_9, xnor_1_out, xnor_2_out, xnor_3_out, xnor_4_out);
endmodule

module Multiplexer_Logic (
  input  in_1,
  input  in_2,
  input  in_3,
  input  in_4,
  input  in_5,
  input  in_6,
  input  in_7,
  input  in_8,
  input  in_9,
  output out_10,
  output out_11,
  output out_12,
  output out_13
);

  Multiplexer multiplexer_1 (.in0(in_1), .in1(in_2), .out(out_10), .sel(in_9));  // open: en
  Multiplexer multiplexer_2 (.in0(in_3), .in1(in_4), .out(out_11), .sel(in_9));  // open: en
  Multiplexer multiplexer_3 (.in0(in_5), .in1(in_6), .out(out_12), .sel(in_9));  // open: en
  Multiplexer multiplexer_4 (.in0(in_7), .in1(in_8), .out(out_13), .sel(in_9));  // open: en
endmodule
